# Fritzing sketch Untitled Sketch 2 (saved by Fritzing 0.9.3b)
breadboards: 1

parts:
  LED1 = LED - 5mm [color="Green (555nm)" package="5 mm [THT]"]
  Raspberry_Pi_ＧＰＩＯ1 = AE-RBPI-BOB40KIT
  J1 = Basic Servo

nets:
  GND: LED1.cathode, Raspberry_Pi_ＧＰＩＯ1.GND, J1.gnd
  N1: LED1.anode, Raspberry_Pi_ＧＰＩＯ1.GPIO19
  N2: Raspberry_Pi_ＧＰＩＯ1.GPIO13, J1.pulse
  +5V: Raspberry_Pi_ＧＰＩＯ1.+5V, J1.vcc

custom parts:
  AE-RBPI-BOB40KIT: http://akizukidenshi.com/catalog/g/gK-08892/
